# Fritzing sketch myco_main (saved by Fritzing 0.9.2b)
breadboards: 1

parts:
  U1 = atmega328 [package=dip]
  R1 = Resistor [tolerance=±5% resistance=1M package=THT]
  LLC = Logic Level Converter
  XTAL1 = Crystal [frequency="16 Mhz" package=THT]
  C1 = Ceramic Capacitor [capacitance=20pF package="100 mil [THT, multilayer]"]
  C2 = Ceramic Capacitor [capacitance=20pF package="100 mil [THT, multilayer]"]
  MD1 = IC, SIP package, 8 pins [chip_label=BA6208]
  C1_2 = IC, DIP package, 10 pins [chip_label=TCS230]
  M1 = DC Motor
  LM3940 = Voltage Regulator - 3.3V [package="TO220 [THT]"]
  C3 = Ceramic Capacitor [capacitance=100pF package="100 mil [THT, multilayer]"]
  C4 = Ceramic Capacitor [capacitance=100pF package="100 mil [THT, multilayer]"]
  BLE1 = IC, DIP package, 4 pins [chip_label=BLE]
  IC1 = IC, SIP package, 3 pins [chip_label=LM35DZ]
  R2 = Resistor [tolerance=±5% resistance=1M package=THT]

nets:
  N1: U1.RESET, R1.Pin_1
  N2: U1.D0_(RX), LLC.RX_LV
  N3: U1.D1_(TX), LLC.TX_HV
  External Interrupt: U1.D2, R2.Pin_1
  5V: U1.VCC, R1.Pin_0, LLC.HV, MD1.pin6, IC1.pin1
  GND: U1.GND, LLC.GND, C1.0, C2.0, MD1.pin5, C1_2.pin2, C1_2.pin3, C1_2.pin4, C1_2.pin8, C1_2.pin9, M1.pin_2, LM3940.GND, C3.0, C4.0, BLE1.pin2, IC1.pin3, R2.Pin_0
  N4: U1.XLAT1, XTAL1.pin_0, C1.1
  N5: U1.XLAT2, XTAL1.pin_1, C2.1
  N6: U1.D8, C1_2.pin5
  N7: U1.D9_(PWM), MD1.pin4
  N8: U1.D10_(PWM), MD1.pin3
  LiPo Batt Voltage: U1.A0
  N9: U1.A1, IC1.pin2
  N10: LLC.LV, LM3940.output_voltage, C4.1
  N11: LLC.TX_LV, BLE1.pin4
  N12: LLC.RX_HV, BLE1.pin3
  N13: MD1.pin7, C1_2.pin1, C1_2.pin10, LM3940.input_voltage, C3.1
  N14: MD1.pin8, M1.pin_1
  3.3V: BLE1.pin1

notes:
  Coin Cell
