# Fritzing sketch MYCO-Polling (saved by Fritzing 0.9.2b)
breadboards: 1

parts:
  RTC = Real Time Clock Module - DS1307 RTC Breakout Board
  R1 = Resistor [tolerance=±5% resistance=10k package=THT]
  U1 = mystery part, 6 pins [chip_label=ISP]
  AtTiny2313-20PU2 = IC, DIP package, 20 pins [chip_label=AtTiny2313-20PU]
  U2 = mystery part, 1 pin [chip_label=?]
  R2 = Resistor [tolerance=±5% resistance=10k package=THT]

nets:
  N1: RTC.5V, R1.Pin_0
  GND: RTC.GND, U1.pin2, AtTiny2313-20PU2.pin10
  N2: RTC.SQW, AtTiny2313-20PU2.pin6, R2.Pin_1
  N3: R1.Pin_1, U1.pin3, AtTiny2313-20PU2.pin1
  N4: U1.pin1, AtTiny2313-20PU2.pin20
  N5: U1.pin4, AtTiny2313-20PU2.pin19
  N6: U1.pin5, AtTiny2313-20PU2.pin18
  N7: U1.pin6, AtTiny2313-20PU2.pin17
  N8: AtTiny2313-20PU2.pin9, U2.pin1
  5V: R2.Pin_0
